# Fritzing sketch Diagram (saved by Fritzing 0.9.3b)

parts:
  U1 = RELAY [package=relay-jzc]
  R1 = Resistor [tolerance=±5% resistance=220 package=THT]
  Q1 = NPN-Transistor [package="TO92 [THT]"]
  D1 = Rectifier Diode [part_number=1N4001 package="300 mil [THT]"]
  R2 = Photocell (LDR) [package=THT]
  VCC1 = Battery
  JP1 = Header 2 [package=screwterminal-3.5mm-2_lock]
  LED1 = LED - 5mm [color="Red (633nm)" package="5 mm [THT]"]
  Power_plug1 = Power plug

nets:
  N1: U1.COIL2, R1.Pin_0, VCC1.+
  N2: U1.NC, JP1.1, LED1.cathode
  N3: U1.NO, Q1.E, D1.anode
  N4: U1.COIL1, JP1.2, Power_plug1.VCC
  N5: R1.Pin_1, R2.pin_0
  N6: LED1.anode, Power_plug1.GND
